# Fritzing sketch Fritzing (saved by Fritzing 0.9.9b)
breadboards: 1

parts:
  MCU1 = Raspberry Pi Zero
  U1 = MAX6675 [package=so08]
  U2 = MAX6675 [package=so08]
  U3 = RELAY-SOLIDSTATE [package=relay-s108t02]  # not connected
  U4 = RELAY-SOLIDSTATE [package=relay-s108t02]  # not connected

nets:
  VDD: MCU1.pin_1, MCU1.pin_17, U1.VDD, U2.VDD
  VSS: MCU1.pin_9, MCU1.pin_39, U1.VSS, U2.VSS
  N1: MCU1.pin_21, U1.MISO, U2.MISO
  N2: MCU1.pin_23, U1.SCK, U2.SCK
  N3: MCU1.pin_24, U1.CS
  N4: MCU1.pin_26, U2.CS
